// Logisim project 6502_computer.circ as structural Verilog: 1 circuit, main circuit main
module main (
);

  wire button_1_out, clock_1_out, w65c02s_pdip_40_1_p17, w65c02s_pdip_40_1_p21;
  wire [7:0] w65c02s_pdip_40_1_p22;
  wire [11:0] w65c02s_pdip_40_1_p5;
  wire [15:12] w65c02s_pdip_40_1_p30;

  Clock clock_1 (.out(clock_1_out));
  // W65C02S__PDIP_40 w65c02s_pdip_40_1: pin names not known; wires that end beside it: 1'b1, 1'b1, 1'b1, 1'b1, w65c02s_pdip_40_1_p5[0], w65c02s_pdip_40_1_p5[1], w65c02s_pdip_40_1_p5[2], w65c02s_pdip_40_1_p5[3], w65c02s_pdip_40_1_p5[4], w65c02s_pdip_40_1_p5[5], w65c02s_pdip_40_1_p5[6], w65c02s_pdip_40_1_p5[7], w65c02s_pdip_40_1_p5[8], w65c02s_pdip_40_1_p5[9], w65c02s_pdip_40_1_p5[10], w65c02s_pdip_40_1_p5[11], w65c02s_pdip_40_1_p17, 1'b1, clock_1_out, 1'b1, w65c02s_pdip_40_1_p21, w65c02s_pdip_40_1_p22[0], w65c02s_pdip_40_1_p22[1], w65c02s_pdip_40_1_p22[2], w65c02s_pdip_40_1_p22[3], w65c02s_pdip_40_1_p22[4], w65c02s_pdip_40_1_p22[5], w65c02s_pdip_40_1_p22[6], w65c02s_pdip_40_1_p22[7], w65c02s_pdip_40_1_p30[15], w65c02s_pdip_40_1_p30[14], w65c02s_pdip_40_1_p30[13], w65c02s_pdip_40_1_p30[12], 1'b0
  // Probe on {w65c02s_pdip_40_1_p30, w65c02s_pdip_40_1_p5}
  Pull_Resistor #(.pull(1)) pull_resistor_1 (.node(w65c02s_pdip_40_1_p17));
  // Probe on w65c02s_pdip_40_1_p21
  not not_1 (w65c02s_pdip_40_1_p17, button_1_out);
  Button button_1 (.out(button_1_out));
  ROM #(.addrWidth(15)) rom_1 (
    .addr({w65c02s_pdip_40_1_p30[14:12], w65c02s_pdip_40_1_p5}), .data(w65c02s_pdip_40_1_p22),
    .sel(w65c02s_pdip_40_1_p30[15]));
  // Probe on w65c02s_pdip_40_1_p22

  // Notes on the sheet:
  //   contents of rom_1 (hex, n*v repeats v):
  //   4c 0 80 32762*0 80
endmodule
